# Fritzing sketch ARDUINO-L293D-2MOTOR-DRIVE (saved by Fritzing 0.7.4b)
breadboards: 1

parts:
  U1 = Arduino Mega
  IC1 = L293D [package=THT]
  M1 = DC Motor
  M2 = DC Motor
  VCC1 = Battery  # not connected
  VCC2 = Battery  # not connected
  VCC3 = Battery  # not connected
  R1 = Resistor [tolerance=±5% resistance=150 package=THT]
  LED1 = LED - 5mm [color="Yellow (595nm)" package="5 mm [THT]"]
  LED2 = LED - 5mm [color="Yellow (595nm)" package="5 mm [THT]"]

nets:
  N1: U1.GND, IC1.0V, LED1.cathode
  N2: U1.D7, R1.Pin_1
  N3: U1.D6, IC1.In_2
  N4: U1.D5, IC1.In_1
  N5: U1.D4, IC1.In_4
  N6: U1.D3, IC1.In_3
  N7: U1.D2, IC1.Enable_1, IC1.Enable_2
  N8: U1.+5V, IC1.+V
  N9: U1.VIN, IC1.+Vmotor
  N10: IC1.Out_1_(_Controlled_by_Enable_1_), M2.pin_2
  N11: IC1.Out_2_(_Controlled_by_Enable_1_), M2.pin_1
  N12: IC1.Out_3_(_Controlled_by_Enable_2_), M1.pin_2
  N13: IC1.Out_4_(_Controlled_by_Enable_2_), M1.pin_1
  N14: R1.Pin_0, LED2.anode
  N15: LED1.anode, LED2.cathode

notes:
  car headlights
  car traction motor
  car steering motor
  battery pack 7,2 V
